// Digital circuit Counter16.dig as structural Verilog
module Counter16 (
  input  nPL,
  input  nU_D,
  input  CP,
  input  nCE,
  input  [15:0] In,
  output [15:0] Out,
  output nRC
);

  wire _74191_1_p15, _74191_2_p15, _74191_3_p15;

  // _74191 _74191_1: pin names not known; wires that end beside it: In[0], nPL, nU_D, CP, nCE, In[1], In[2], In[3], 1'b1, 1'b0, Out[0], Out[1], Out[2], Out[3], _74191_1_p15
  // _74191 _74191_2: pin names not known; wires that end beside it: In[4], nPL, nU_D, CP, _74191_1_p15, In[5], In[6], In[7], 1'b1, 1'b0, Out[4], Out[5], Out[6], Out[7], _74191_2_p15
  // _74191 _74191_3: pin names not known; wires that end beside it: In[8], nPL, nU_D, CP, _74191_2_p15, In[9], In[10], In[11], 1'b1, 1'b0, Out[8], Out[9], Out[10], Out[11], _74191_3_p15
  // _74191 _74191_4: pin names not known; wires that end beside it: In[12], nPL, nU_D, CP, _74191_3_p15, In[13], In[14], In[15], 1'b1, 1'b0, Out[12], Out[13], Out[14], Out[15], nRC
endmodule
